# Fritzing sketch dioderctrl (saved by Fritzing 0.9.0b)
breadboards: 1

parts:
  Bauteil1 = Spark Core (v1.0)
  IC2 = ULN2003A [package="SO16 [SMD]"]
  J2 = female pin header, 5 pins [form="♀ (female)"]
  IC3 = Voltage Regulator [package=to220-igo]
  C1 = Electrolytic Capacitor [capacitance=1µF package="1010 [SMD, electrolytic]"]
  C2 = Electrolytic Capacitor [capacitance=0.47mF package="1010 [SMD, electrolytic]"]  # not connected

nets:
  N1: Bauteil1.A5, IC2.Out_6
  N2: Bauteil1.A6, IC2.COM_-_Common
  N3: Bauteil1.A7, IC2.Out_7
  N4: Bauteil1.GND, IC2.Out_1, J2.pin5, IC3.IN, C1.-
  N5: Bauteil1.VIN, IC3.OUT, C1.+
  N6: IC2.In_6, J2.pin2
  N7: IC2.In_7, J2.pin3
  N8: IC2.0V, J2.pin4
  N9: J2.pin1, IC3.GND

notes:
  DIODER Power distributor
